# Fritzing sketch image.png (saved by Fritzing 1.0.6)
breadboards: 1

parts:
  Q1 = PNP-Transistor [package="TO92 [THT]"]
  Componente1 = Arduino Uno (Rev3)
  LED1 = RGB LED - (4 legs) [color="Red (633nm)" current=0.030A package="5 mm [THT]"]
  Q2 = PNP-Transistor [package="TO92 [THT]"]
  Q3 = PNP-Transistor [package="TO92 [THT]"]
  R1 = Resistor [tolerance=±5% resistance=220 package="0805 [SMD]"]
  R2 = Resistor [tolerance=±5% resistance=220 package="0805 [SMD]"]
  R3 = Resistor [tolerance=±5% resistance=220 package="0805 [SMD]"]

nets:
  N1: Q1.E, R3.Pin_0
  N2: Q1.B, Componente1.D3_PWM
  N3: Q1.C, Componente1.GND, Q2.C, Q3.C
  N4: Componente1.D1/TX, Q2.B
  N5: Componente1.D2, Q3.B
  N6: LED1.red_cathode, R1.Pin_1
  N7: LED1.green_cathode, R2.Pin_1
  N8: LED1.blue_cathode, R3.Pin_1
  N9: Q2.E, R1.Pin_0
  N10: Q3.E, R2.Pin_0
